// Logisim project CPU.circ as structural Verilog: 5 circuits, main circuit ALUExtend1
module ALUExtend1 (
  input  a,
  input  b,
  input  [2:0] xyz,
  output ia,
  output ib
);

  wire and_1_out, not_1_out, or_1_out, xor_1_out;
  wire [1:1] or_2_out;

  and and_1 (and_1_out, a, b);
  or or_1 (or_1_out, a, b);
  xor xor_1 (xor_1_out, a, b);
  Multiplexer #(.select(2), .enable("false")) multiplexer_1 (
    .in0(and_1_out), .in1(or_1_out), .in2(a), .in3(xor_1_out), .out(ia), .sel({or_2_out[1], xyz[0]}));
  or or_2 (or_2_out[1], xyz[2], xyz[1]);
  not not_1 (not_1_out, xyz[0]);
  and and_2 (ib, b, not_1_out, xyz[1]);
endmodule

module ALUExtend2 (
  input  [1:0] a,
  input  [1:0] b,
  input  [2:0] xyz,
  output [1:0] ia,
  output [1:0] ib
);

  ALUExtend1 aluextend1_1 (.a(a[0]), .b(b[0]), .xyz(xyz), .ia(ia[0]), .ib(ib[0]));
  ALUExtend1 aluextend1_2 (.a(a[1]), .b(b[1]), .xyz(xyz), .ia(ia[1]), .ib(ib[1]));
endmodule

module ALUExtend4 (
  input  [3:0] a,
  input  [3:0] b,
  input  [2:0] xyz,
  output [3:0] ia,
  output [3:0] ib
);

  ALUExtend2 aluextend2_1 (.a(a[1:0]), .b(b[1:0]), .xyz(xyz), .ia(ia[1:0]), .ib(ib[1:0]));
  ALUExtend2 aluextend2_2 (.a(a[3:2]), .b(b[3:2]), .xyz(xyz), .ia(ia[3:2]), .ib(ib[3:2]));
endmodule

module ALUExtend8 (
  input  [7:0] a,
  input  [7:0] b,
  input  [2:0] xyz,
  output [7:0] ia,
  output [7:0] ib
);

  ALUExtend4 aluextend4_1 (.a(a[3:0]), .b(b[3:0]), .xyz(xyz), .ia(ia[3:0]), .ib(ib[3:0]));
  ALUExtend4 aluextend4_2 (.a(a[7:4]), .b(b[7:4]), .xyz(xyz), .ia(ia[7:4]), .ib(ib[7:4]));
endmodule

module ALU (
  input  [2:0] xyz,
  input  [17:0] a,
  input  [17:0] b,
  output [17:0] out
);

  wire [1:0] aluextend2_1_ia, aluextend2_1_ib;
  wire [7:0] aluextend8_1_ia, aluextend8_1_ib, aluextend8_2_ia, aluextend8_2_ib;

  ALUExtend8 aluextend8_1 (.a(a[7:0]), .b(b[7:0]), .xyz(xyz), .ia(aluextend8_1_ia), .ib(aluextend8_1_ib));
  ALUExtend8 aluextend8_2 (.a(a[15:8]), .b(b[15:8]), .xyz(xyz), .ia(aluextend8_2_ia), .ib(aluextend8_2_ib));
  ALUExtend2 aluextend2_1 (.a(a[17:16]), .b(b[17:16]), .xyz(xyz), .ia(aluextend2_1_ia), .ib(aluextend2_1_ib));
  Adder #(.width(18)) adder_1 (
    .a({aluextend2_1_ia, aluextend8_2_ia, aluextend8_1_ia}),
    .b({aluextend2_1_ib, aluextend8_2_ib, aluextend8_1_ib}), .out(out), .cin(xyz[2]));  // open: cout
endmodule
